# Fritzing sketch Stripboard_49x18 (saved by Fritzing 0.9.6b)
stripboards: 1

parts:
  J3_Besat_Test = male pin header, 2 pins [form="♂ (male)"]
  R1 = Resistor [tolerance=±5% power=0.25 resistance=2.2k package=THT]
  D1 = Rectifier Diode [part_number=1N4001 package="300 mil [THT]"]
  D2 = Rectifier Diode [part_number=1N4001 package="300 mil [THT]"]
  R2 = Resistor [tolerance=±5% power=0.25 resistance=10 package=THT]
  Q1 = PNP-Transistor [part_number=BC557 package="TO92 [THT]"]
  J4_DCC_GND = male pin header, 4 pins [form="♂ (male)"]
  R3 = Resistor [tolerance=±5% power=0.25 resistance=1.5k package=THT]
  J5_DCC_In = male pin header, 4 pins [form="♂ (male)"]
  J7_3V3 = male pin header, 4 pins [form="♂ (male)"]
  U1 = Optocoupler [package=THT]
  J8 = male pin header, 4 pins [form="♂ (male)"]
  J9 = male pin header, 4 pins [form="♂ (male)"]
  C2 = Tantalum Capacitor [capacitance=1μF voltage=35V package="100 mil [THT, tantalum]"]
  D4 = Schottky Diode [part_number=1N5817 package="300 mil [THT]"]
  D5 = Schottky Diode [part_number=1N5817 package="300 mil [THT]"]
  Q2 = NPN-Transistor [part_number=BC547 package="TO92 [THT]"]
  R6 = Resistor [tolerance=±5% power=0.25 resistance=10k package=THT]
  R7 = Resistor [tolerance=±5% power=0.25 resistance=10k package=THT]
  J10_TEST = male pin header, 1 pin [form="♂ (male)"]
  LED1 = LED - 5mm [color="Red (633nm)" current=0.030 package="5 mm [THT]"]
  C3 = Ceramic Capacitor [capacitance=22nF voltage=35V package="100 mil [THT, multilayer]"]
  R8 = Resistor [tolerance=±5% power=0.25 resistance=10k package=THT]
  J10_DCC_Track = male pin header, 2 pins [form="♂ (male)"]

nets:
  N1: J3_Besat_Test.pin1, J3_Besat_Test.pin2, R1.Pin_0
  N2: R1.Pin_1, D1.anode, D2.cathode, R2.Pin_0, J10_DCC_Track.pin1, J10_DCC_Track.pin2
  N3: D1.cathode, D2.anode, Q1.E, J5_DCC_In.pin1, J5_DCC_In.pin2, J5_DCC_In.pin3, J5_DCC_In.pin4, D5.anode
  N4: R2.Pin_1, Q1.B
  N5: Q1.C, D4.anode
  N6: J4_DCC_GND.pin1, J4_DCC_GND.pin2, J4_DCC_GND.pin3, J4_DCC_GND.pin4, J8.pin1, J8.pin2, J8.pin3, J8.pin4, C2.-, Q2.E, C3.0, R8.Pin_1
  N7: R3.Pin_0, C2.+, D5.cathode
  N8: R3.Pin_1, LED1.anode
  N9: J7_3V3.pin1, J7_3V3.pin2, J7_3V3.pin3, J7_3V3.pin4, R7.Pin_1
  N10: U1.Pin_1, LED1.cathode
  N11: U1.Pin_2, Q2.C
  N12: U1.Pin_4, J9.pin1, J9.pin2, J9.pin3, J9.pin4
  N13: U1.Pin_5, R7.Pin_0, J10_TEST.pin1
  N14: D4.cathode, R6.Pin_0, C3.1, R8.Pin_0
  N15: Q2.B, R6.Pin_1

notes:
  DCC
  3v3
